# Fritzing sketch MainBoardRadio_v2 (saved by Fritzing 0.9.4)
breadboards: 1

parts:
  U2 = DOIT Esp32 DevKit v1 (30 pins long, 11 pins width) [part_number=ESP32S-PIN30]
  Amplifier_TPA3116D2 = male pin header, 10 pins [form="♂ (male)"]  # not connected
  U4 = 3.5mm Audio Jack [package=audio-jack]  # not connected
  Snooze_btn = male pin header, 2 pins [form="♂ (male)"]
  VS1053_MP3_decoder = male pin header, 10 pins [form="♂ (male)"]
  Switchboard = male pin header, 11 pins [form="♂ (male)" part_number=Switchboard]
  Power_supply = male pin header, 2 pins [form="♂ (male)"]
  J6-TFT = male pin header, 9 pins [form="♂ (male)"]

nets:
  N1: U2.GND, Snooze_btn.pin2, VS1053_MP3_decoder.pin9, Switchboard.pin10, Power_supply.pin1, J6-TFT.pin2
  N2: U2.D2, J6-TFT.pin5
  N3: U2.D4, Switchboard.pin6
  N4: U2.RX2, Snooze_btn.pin1
  N5: U2.TX2, Switchboard.pin5
  N6: U2.D5, Switchboard.pin8
  N7: U2.D18, VS1053_MP3_decoder.pin5, J6-TFT.pin7
  N8: U2.D19, VS1053_MP3_decoder.pin7, J6-TFT.pin9
  N9: U2.D21, Switchboard.pin7
  N10: U2.D22, J6-TFT.pin8
  N11: U2.D23, VS1053_MP3_decoder.pin6, J6-TFT.pin6
  N12: U2.EN, VS1053_MP3_decoder.pin3, J6-TFT.pin4
  N13: U2.VP, Switchboard.pin3
  N14: U2.VN, Switchboard.pin2
  N15: U2.D34, Switchboard.pin1
  N16: U2.D35, Switchboard.pin4
  N17: U2.D32, J6-TFT.pin3
  N18: U2.D33, Switchboard.pin9
  N19: U2.D25, VS1053_MP3_decoder.pin4
  N20: U2.D26, VS1053_MP3_decoder.pin1
  N21: U2.VIN, VS1053_MP3_decoder.pin10, Switchboard.pin11, Power_supply.pin2, J6-TFT.pin1

custom parts:
  DOIT Esp32 DevKit v1 (30 pins long, 11 pins width): The DOIT Esp32 DevKit v1 is one of the development board created by DOIT to evaluate the ESP-WROOM-32 module. It is based on the ESP32 microcontroller that boasts Wifi, Bluetooth, Ethernet and Low Power support all in a single chip. (vanepp) made breadboard work, adjusted pin numbering and labels and reduced size of schematic and cleaned up pcb. This chip is 30pins long (2 x15) and 11 pins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
